// Logisim project universal_shift_register.circ as structural Verilog: 1 circuit, main circuit main
module main (
  input  I3,
  input  I2,
  input  I1,
  input  I0,
  input  R,
  input  L,
  input  [1:0] S,
  input  PRESET,
  input  CLR,
  output Q3,
  output Q2,
  output Q1,
  output Q0
);

  wire CLK_out, multiplexer_1_out, multiplexer_2_out, multiplexer_3_out, multiplexer_4_out;

  Clock CLK (.out(CLK_out));
  Multiplexer #(.select(2)) multiplexer_1 (.in0(Q3), .in1(R), .in2(Q2), .in3(I3), .out(multiplexer_1_out), .sel(S));
  D_Flip_Flop d_ff_1 (.D(multiplexer_1_out), .clk(CLK_out), .Q(Q3), .preset(PRESET), .reset(CLR));  // open: Qn
  Multiplexer #(.select(2)) multiplexer_2 (.in0(Q2), .in1(Q3), .in2(Q1), .in3(I2), .out(multiplexer_2_out), .sel(S));
  D_Flip_Flop d_ff_2 (.D(multiplexer_2_out), .clk(CLK_out), .Q(Q2), .preset(PRESET), .reset(CLR));  // open: Qn
  Multiplexer #(.select(2)) multiplexer_3 (.in0(Q1), .in1(Q2), .in2(Q0), .in3(I1), .out(multiplexer_3_out), .sel(S));
  D_Flip_Flop d_ff_3 (.D(multiplexer_3_out), .clk(CLK_out), .Q(Q1), .preset(PRESET), .reset(CLR));  // open: Qn
  Multiplexer #(.select(2)) multiplexer_4 (.in0(Q0), .in1(Q1), .in2(L), .in3(I0), .out(multiplexer_4_out), .sel(S));
  D_Flip_Flop d_ff_4 (.D(multiplexer_4_out), .clk(CLK_out), .Q(Q0), .preset(PRESET), .reset(CLR));  // open: Qn
endmodule
